# Fritzing sketch Monitoring (saved by Fritzing 0.9.2b)

parts:
  Part2 = Arduino Mega 2560 (Rev3)
  BH1750FVI_Breakout1 = BH1750 (GY-302) Breakout Board [part_number=BH1750FVI]
  DHT1 = DHT22 Humidity and Temperature Sensor
  DHT2 = DHT22 Humidity and Temperature Sensor
  DHT3 = DHT11 Humitidy and Temperature Sensor
  U1 = MAX6675 [package=so08]
  U2 = MAX6675 [package=so08]
  U3 = MAX6675 [package=so08]
  U4 = MAX6675 [package=so08]
  DHT4 = DHT22 Humidity and Temperature Sensor
  DHT5 = DHT22 Humidity and Temperature Sensor
  sdCard1 = my_sdCard

nets:
  N1: Part2.D21/SCL, BH1750FVI_Breakout1.SCL
  N2: Part2.D20/SDA, BH1750FVI_Breakout1.SDA
  3V3: Part2.3V3, BH1750FVI_Breakout1.VCC
  5V: Part2.5V, U1.VDD
  GND: Part2.GND, U1.VSS
  N3: Part2.D2_PWM, DHT2.DATA
  N4: Part2.D3_PWM, DHT1.DATA
  N5: Part2.D4_PWM, DHT5.DATA
  N6: Part2.D5_PWM, DHT4.DATA
  N7: Part2.D7_PWM, DHT3.DATA
  N8: Part2.D22, U4.MISO
  N9: Part2.D23, U1.SCK
  N10: Part2.D24, U4.CS
  N11: Part2.D25, U1.CS
  N12: Part2.D26, U4.SCK
  N13: Part2.D27, U1.MISO
  N14: Part2.D28, U3.MISO
  N15: Part2.D29, U2.SCK
  N16: Part2.D30, U3.CS
  N17: Part2.D31, U2.CS
  N18: Part2.D32, U3.SCK
  N19: Part2.D33, U2.MISO
  N20: Part2.D50, sdCard1.MISO
  N21: Part2.D51, sdCard1.MOSI
  N22: Part2.D52, sdCard1.SCK
  N23: Part2.D53, sdCard1.CS

custom parts:
  BH1750 (GY-302) Breakout Board: The ROHM Semiconductor BH1750FVI is a digital ambient light sensor for the I2C bus interface. The BH750FVI is able to detect a wide range of light intensities (1-65535 lux). The spectral range is similar to that of the human eye.
  DHT11 Humitidy and Temperature Sensor: DHT11 Humidity and Temperature Sensor
  my_sdCard: micro sdCard Adapter with 90º pin header. Use a filtering Capacitor between CS and GND if needed. PCB View Pinouts are Reversed for laying parallel on PCB using a 90º pin header.
